# Fritzing sketch espac (saved by Fritzing 0.9.4)
breadboards: 1

parts:
  WeMos_D1_Mini1 = WeMos D1 Mini
  BME280 = BME280 Breakout
  ZS-042_RTC1 = ZS-042 RTC Module
  D1 = LTE-302 [part_number="940nm IR" package=lte-302]
  R1 = Resistor [tolerance=±5% resistance=220 package="0402 [SMD]"]
  LED1 = LED - 3mm [color="Blue (525nm)" package="3 mm [THT]"]
  Q1 = PNP-Transistor [part_number=2222A package="TO92 [THT]"]

nets:
  3V3: WeMos_D1_Mini1.3V3, BME280.3.3V
  5V: WeMos_D1_Mini1.5V, ZS-042_RTC1.VCC, Q1.E
  N1: WeMos_D1_Mini1.D0, R1.Pin_0
  N2: WeMos_D1_Mini1.D1, BME280.SCK/SCL
  N3: WeMos_D1_Mini1.D2, BME280.SDI/SDA, ZS-042_RTC1.SDA
  N4: WeMos_D1_Mini1.D5, Q1.B
  GND: WeMos_D1_Mini1.G, BME280.GND, ZS-042_RTC1.GND, D1.C, LED1.cathode
  N5: D1.A, Q1.C
  N6: R1.Pin_1, LED1.anode
